# Fritzing sketch Fritzing_sketch (saved by Fritzing 0.9.6b)

parts:
  Pico = Raspberry Pi Pico H
  A1 = Waveshare e-Paper HAT [package=THT]
  Btn = Arcade Button (white)
  LED1 = LEDs [package=led10mm]
  Sw1 = Momentary Switch [package=ksa_sealed_tac_switch]
  R1 = Resistor [tolerance=±5% resistance=220 package="2010 [SMD]"]
  Sw2 = Momentary Switch [package=ksa_sealed_tac_switch]
  Sw3 = Momentary Switch [package=ksa_sealed_tac_switch]
  Printer_TTY = JST-B3P-VH [part_number=JST-B3P-VH package=THT]
  Printer_Pwr = JST-B3P-VH [part_number=JST-B3P-VH package=THT]

nets (from the breadboard view):
  N1: Pico.VSYS, A1.pin_8, Printer_Pwr.pin3
  N2: Pico.GND, A1.pin_7, LED1.C, Printer_TTY.pin3, Printer_Pwr.pin1
  N3: Pico.3V3, Btn.no_name_yet#1, Sw1.1, Sw2.1, Sw3.1
  N4: Pico.GP20, Sw1.2
  N5: Pico.GP19, Sw2.2
  N6: Pico.GP18, Sw3.2
  N7: Pico.GP17, Btn.no_name_yet#2
  N8: Pico.GP16, R1.Pin_1
  N9: Pico.GP13, A1.pin_1
  N10: Pico.GP12, A1.pin_2
  N11: Pico.GP11, A1.pin_6
  N12: Pico.GP10, A1.pin_5
  N13: Pico.GP9, A1.pin_4
  N14: Pico.GP8, A1.pin_3
  N15: Pico.GP1, Printer_TTY.pin2
  N16: Pico.GP0, Printer_TTY.pin1
  N17: LED1.A, R1.Pin_0

notes:
  Printer TTY
  Printer Power
  Arcade LED Button
  Raspberry Pi Pico
  Waveshare e-Paper Hat
  Tactile Button Array

custom parts:
  Raspberry Pi Pico H: Raspberry Pi Pico H. Based around the RP2040 microcontroller the Pico H is a low cost microcontroller device bringing Raspberry Pi quality, cost, and easy of use to the microcontroller space.
  Waveshare e-Paper HAT: .This is a universal driver board for e-Paper raw panels, can be used to drive various SPI interface e-Paper from Waveshare.
  Arcade Button (white): Adafruit Arcade Button (white)
